// Logisim project 1 Bit ALU.circ as structural Verilog: 1 circuit, main circuit main
module main (
  input  in_1,
  input  in_2,
  input  in_3,
  input  [1:0] in_4,
  output out_5,
  output out_6
);

  wire adder_1_out, and_1_out, nor_1_out, xor_1_out;

  Adder #(.width(1)) adder_1 (.a(in_2), .b(in_1), .out(adder_1_out), .cin(in_3), .cout(out_5));
  and and_1 (and_1_out, in_2, in_1);
  nor nor_1 (nor_1_out, in_2, in_1);
  xor xor_1 (xor_1_out, in_2, in_1);
  Multiplexer #(.select(2), .enable("false")) multiplexer_1 (
    .in0(adder_1_out), .in1(and_1_out), .in2(nor_1_out), .in3(xor_1_out), .out(out_6), .sel(in_4));
endmodule
