// Logisim project 1,3,5,6 Sequence Genrator Using Counter.circ as structural Verilog: 1 circuit, main circuit main
module main (
  input  in_1,
  input  in_2,
  input  in_3,
  input  in_4,
  input  in_5,
  input  in_6,
  output out_7,
  output out_8,
  output out_9
);

  wire and_1_out, and_2_out, clock_1_out, j_k_ff_2_qn, j_k_ff_3_qn, or_1_out;

  Clock clock_1 (.out(clock_1_out));
  and and_1 (and_1_out, out_8, out_9);
  J_K_Flip_Flop j_k_ff_1 (
    .J(and_1_out), .clk(clock_1_out), .K(or_1_out), .Q(out_7), .preset(in_1), .reset(in_2));  // open: Qn, en
  J_K_Flip_Flop j_k_ff_2 (
    .J(out_9), .clk(clock_1_out), .K(1'b1), .Q(out_8), .Qn(j_k_ff_2_qn), .preset(in_3), .reset(in_4));  // open: en
  or or_1 (or_1_out, out_8, j_k_ff_3_qn);
  and and_2 (and_2_out, j_k_ff_2_qn, out_7);
  J_K_Flip_Flop j_k_ff_3 (
    .J(1'b1), .clk(clock_1_out), .K(and_2_out), .Q(out_9), .Qn(j_k_ff_3_qn), .preset(in_5), .reset(in_6));  // open: en
endmodule
