// Logisim project 4 Bit Synchronus Down Counter.circ as structural Verilog: 1 circuit, main circuit main
module main (
  output out_1,
  output out_2,
  output out_3,
  output out_4
);

  wire and_1_out, and_2_out, clock_1_out, j_k_ff_1_qn, j_k_ff_2_qn, j_k_ff_3_qn;

  Clock clock_1 (.out(clock_1_out));
  J_K_Flip_Flop j_k_ff_1 (
    .J(1'b1), .clk(clock_1_out), .K(1'b1), .Q(out_4), .Qn(j_k_ff_1_qn));  // open: preset, en, reset
  J_K_Flip_Flop j_k_ff_2 (
    .J(j_k_ff_1_qn), .clk(clock_1_out), .K(j_k_ff_1_qn), .Q(out_3), .Qn(j_k_ff_2_qn));  // open: preset, en, reset
  and and_1 (and_1_out, j_k_ff_2_qn, j_k_ff_1_qn);
  J_K_Flip_Flop j_k_ff_3 (
    .J(and_1_out), .clk(clock_1_out), .K(and_1_out), .Q(out_2), .Qn(j_k_ff_3_qn));  // open: preset, en, reset
  and and_2 (and_2_out, j_k_ff_3_qn, and_1_out);
  J_K_Flip_Flop j_k_ff_4 (.J(and_2_out), .clk(clock_1_out), .K(and_2_out), .Q(out_1));  // open: Qn, preset, en, reset

  // Notes on the sheet:
  //   4 bit synchronus down counter
endmodule
