// Logisim project Bi Directional Shift Register.circ as structural Verilog: 1 circuit, main circuit main
module main (
  input  in_1,
  input  in_2,
  input  in_3,
  input  in_4,
  input  in_5,
  input  in_6,
  input  in_7,
  input  in_8,
  input  Data_Left,
  input  Data_Right,
  input  in_11,
  output out_12,
  output out_13,
  output out_14,
  output out_15
);

  wire and_1_out, and_2_out, and_3_out, and_4_out, and_5_out, and_6_out, and_7_out, and_8_out, clock_1_out,
       not_1_out, or_1_out, or_2_out, or_3_out, or_4_out;

  Clock clock_1 (.out(clock_1_out));
  and and_1 (and_1_out, Data_Right, in_11);
  and and_2 (and_2_out, out_13, not_1_out);
  not not_1 (not_1_out, in_11);
  or or_1 (or_1_out, and_1_out, and_2_out);
  and and_3 (and_3_out, out_12, in_11);
  D_Flip_Flop d_ff_1 (.clk(clock_1_out), .D(or_1_out), .Q(out_12), .preset(in_1), .reset(in_2));  // open: Qn, en
  and and_4 (and_4_out, out_14, not_1_out);
  or or_2 (or_2_out, and_3_out, and_4_out);
  D_Flip_Flop d_ff_2 (.clk(clock_1_out), .D(or_2_out), .Q(out_13), .preset(in_3), .reset(in_4));  // open: Qn, en
  and and_5 (and_5_out, out_13, in_11);
  or or_3 (or_3_out, and_5_out, and_6_out);
  and and_6 (and_6_out, out_15, not_1_out);
  D_Flip_Flop d_ff_3 (.clk(clock_1_out), .D(or_3_out), .Q(out_14), .preset(in_5), .reset(in_6));  // open: Qn, en
  and and_7 (and_7_out, out_14, in_11);
  and and_8 (and_8_out, Data_Left, not_1_out);
  D_Flip_Flop d_ff_4 (.clk(clock_1_out), .D(or_4_out), .Q(out_15), .preset(in_7), .reset(in_8));  // open: Qn, en
  or or_4 (or_4_out, and_7_out, and_8_out);

  // Notes on the sheet:
  //   BY directional shift register
endmodule
