// Logisim project Universal Shift Register Using Mux.circ as structural Verilog: 1 circuit, main circuit main
module main (
  input  [1:0] in_1,
  input  Data_Right,
  input  Data_Left,
  input  I0,
  input  I1,
  input  I2,
  input  I3,
  output out_8,
  output out_9,
  output out_10,
  output out_11
);

  wire clock_1_out, multiplexer_1_out, multiplexer_2_out, multiplexer_3_out, multiplexer_4_out;

  Clock clock_1 (.out(clock_1_out));
  Multiplexer #(.select(2)) multiplexer_1 (
    .in0(out_8), .in1(I0), .in2(Data_Right), .in3(out_9), .out(multiplexer_1_out), .sel(in_1));  // open: en
  D_Flip_Flop d_ff_1 (.clk(clock_1_out), .D(multiplexer_1_out), .Q(out_8));  // open: Qn, preset, en, reset
  D_Flip_Flop d_ff_2 (.clk(clock_1_out), .D(multiplexer_2_out), .Q(out_9));  // open: Qn, preset, en, reset
  Multiplexer #(.select(2)) multiplexer_2 (
    .in0(out_9), .in1(I1), .in2(out_8), .in3(out_10), .out(multiplexer_2_out), .sel(in_1));  // open: en
  Multiplexer #(.select(2)) multiplexer_3 (
    .in0(out_10), .in1(I2), .in2(out_9), .in3(out_11), .out(multiplexer_3_out), .sel(in_1));  // open: en
  D_Flip_Flop d_ff_3 (.clk(clock_1_out), .D(multiplexer_3_out), .Q(out_10));  // open: Qn, preset, en, reset
  Multiplexer #(.select(2)) multiplexer_4 (
    .in0(out_11), .in1(I3), .in2(out_10), .in3(Data_Left), .out(multiplexer_4_out), .sel(in_1));  // open: en
  D_Flip_Flop d_ff_4 (.clk(clock_1_out), .D(multiplexer_4_out), .Q(out_11));  // open: Qn, preset, en, reset

  // Notes on the sheet:
  //   Universal shift register using MUX
endmodule
