// Logisim project Up Down Synchronus Counter.circ as structural Verilog: 1 circuit, main circuit main
module main (
  input  in_1,
  output out_2,
  output out_3,
  output out_4
);

  wire and_1_out, and_2_out, clock_1_out, j_k_ff_2_qn, j_k_ff_3_qn, not_1_out, not_2_out, or_1_out, xor_1_out;

  not not_1 (not_1_out, in_1);
  or or_1 (or_1_out, and_1_out, and_2_out);
  Clock clock_1 (.out(clock_1_out));
  J_K_Flip_Flop j_k_ff_1 (.J(or_1_out), .clk(clock_1_out), .K(or_1_out), .Q(out_2));  // open: Qn, preset, en, reset
  xor xor_1 (xor_1_out, in_1, out_4);
  not not_2 (not_2_out, xor_1_out);
  and and_1 (and_1_out, in_1, out_4, out_3);
  and and_2 (and_2_out, not_1_out, j_k_ff_2_qn, j_k_ff_3_qn);
  J_K_Flip_Flop j_k_ff_2 (
    .J(not_2_out), .clk(clock_1_out), .K(not_2_out), .Q(out_3), .Qn(j_k_ff_2_qn));  // open: preset, en, reset
  J_K_Flip_Flop j_k_ff_3 (
    .J(1'b1), .clk(clock_1_out), .K(1'b1), .Q(out_4), .Qn(j_k_ff_3_qn));  // open: preset, en, reset

  // Notes on the sheet:
  //   Synchronus up/down counter
endmodule
